// Logisim project Ctl_Load_Store.circ as structural Verilog: 1 circuit, main circuit Load_Store
module Load_Store (
  input  Enable,
  input  [15:0] Instruction,
  input  Clk,
  input  Reset,
  input  [31:0] Stack_Pointer,
  output Store,
  output Load,
  output PC_Hold,
  output [2:0] Rmd,
  output [31:0] RAM_Addr
);

  wire and_1_out, d_ff_1_q, d_ff_1_qn;
  wire [31:0] adder_1_out, bit_extender_1_out, bit_extender_2_out;

  Multiplexer #(.width(3)) multiplexer_1 (.in0(3'b000), .in1(Instruction[10:8]), .out(Rmd), .sel(Enable));
  assign bit_extender_1_out = {{24{Instruction[7]}}, Instruction[7:0]};  // Bit_Extender bit_extender_1
  and and_1 (and_1_out, ~d_ff_1_q, Instruction[11]);  // AND_Gate
  Adder #(.width(32)) adder_1 (.a(bit_extender_1_out), .b(Stack_Pointer), .out(adder_1_out));  // open: cin, cout
  assign bit_extender_2_out = {{31{Enable}}, Enable};  // Bit_Extender bit_extender_2
  and and_2 (Store, Enable, ~Instruction[11]);  // AND_Gate
  D_Flip_Flop d_ff_1 (.D(and_1_out), .clk(Clk), .Q(d_ff_1_q), .Qn(d_ff_1_qn), .reset(Reset));  // open: preset
  assign RAM_Addr = adder_1_out & bit_extender_2_out;  // AND_Gate and_3, 32 bits wide
  and and_4 (Load, Enable, Instruction[11], d_ff_1_q);
  and and_5 (PC_Hold, Enable, d_ff_1_qn, Instruction[11]);

  // Other names for the same wires on the sheet: RAM[7:0] = Instruction[7:0]; Rmd_t[2:0] = Instruction[10:8]

  // Notes on the sheet:
  //   Instruction: pull=down
  //   Delay load and hold PC for 1 cycle for the RAM to send out requested data 
endmodule
